# Fritzing sketch Untitled Sketch (saved by Fritzing 0.9.3b)
breadboards: 1

parts:
  Part1 = Arduino Nano (Rev3.0)
  Pololu_A1 = Pololu A4988 [package=SO16]
  VCC1 = Battery block 9V
  M1 = Stepper Motor - Bipolar
  C2 = Electrolytic Capacitor [capacitance=100μF package="0807 [SMD, electrolytic]"]

nets:
  N1: Part1.GND, Pololu_A1.GND#8
  N2: Part1.D2, Pololu_A1.DIR
  N3: Part1.D3, Pololu_A1.STEP
  N4: Part1.D5, Pololu_A1.ENABLE
  5V: Part1.5V, Pololu_A1.VDD
  N5: Pololu_A1.RESET, Pololu_A1.SLEEP
  N6: Pololu_A1.1B, M1.D
  N7: Pololu_A1.1A, M1.B
  N8: Pololu_A1.2A, M1.C
  N9: Pololu_A1.2B, M1.A
  N10: Pololu_A1.GND#14, VCC1.-, C2.-
  N11: Pololu_A1.VMOT, VCC1.+, C2.+
